# Fritzing sketch BrewBench-wiring-diagram (saved by Fritzing 0.9.3b)
breadboards: 1

parts:
  R1 = Resistor [tolerance=±5% resistance=220 package=THT]
  Part1 = Arduino Yun
  R2 = Resistor [tolerance=±5% resistance=220 package=THT]
  R3 = Resistor [tolerance=±5% resistance=220 package=THT]
  U6 = Power Outlet [chip_label=IC package="SIP (Single Inline) [THT]"]
  2_Channel_Relay2 = 2 Channel Power Relay

nets:
  5V: R1.Pin_0, Part1.5V, R2.Pin_0, R3.Pin_0, 2_Channel_Relay2.VCC
  N1: R1.Pin_1, Part1.A0
  N2: Part1.A2, R2.Pin_1
  N3: Part1.A4/SDA, R3.Pin_1
  N4: Part1.D2/SDA, Part1.D2, 2_Channel_Relay2.IN1
  N5: Part1.D4, 2_Channel_Relay2.IN2
  GND: Part1.GND, 2_Channel_Relay2.GND
  N6: U6.hot1, 2_Channel_Relay2.K1-NC
  N7: U6.hot2, 2_Channel_Relay2.K2-NC

notes:
  Hot Liquor
  Mash
  Boil
  10K Resistor
  10K Thermistor
  Heater
  Pump
  < Break Tab
  3 prong plug

custom parts:
  Power Outlet: A standard power outlet. Silver screws are neutral, brass screws are hot. Green screw is ground.
  2 Channel Power Relay: A 2 channel power relay. The module operates at 5V.
